# Fritzing sketch RedboardSPI (saved by Fritzing 0.9.2b)
breadboards: 1

parts:
  Part1 = BME280 Breakout  # not connected
  RedBoard1 = RedBoard [part_number=DEV-11575]
  Part2 = Logic Level Converter

nets:
  N1: RedBoard1.D13, Part2.TX2_HV
  N2: RedBoard1.D12, Part2.RX2_HV
  N3: RedBoard1.D11, Part2.RX_HV
  N4: RedBoard1.D10, Part2.TX_HV
  N5: RedBoard1.3V3, Part2.LV
  N6: RedBoard1.+5V, Part2.HV
  GND: RedBoard1.GND, Part2.GND

custom parts:
  RedBoard: At SparkFun we use many Arduinos and we're always looking for the simplest, most stable one. Each board is a bit different and no one board has everything we want, so we decided to make our own version that combines all our favorite features. The RedBoard combines the simplicity of the UNO's Optiboot bootloader (which is used in the Pro series), the stability of the FTDI (which we all missed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
